# Fritzing sketch Fritzing_Taller_IoT (saved by Fritzing 0.7.0b)

parts:
  DHT1 = DHT11 Humitidy and Temperature Sensor
  NodeMCU_v1 = NodeMCU v3 LoLin [part_number=ESP8266]

nets:
  VDD: DHT1.VDD, NodeMCU_v1.3V3
  N1: DHT1.DATA, NodeMCU_v1.D5
  GND: DHT1.GND, NodeMCU_v1.GND

custom parts:
  DHT11 Humitidy and Temperature Sensor: DHT11 Humidity and Temperature Sensor
  NodeMCU v3 LoLin: NodeMCU v3 LoLin NodeMCU (http://www.nodemcu.com/) is an open source IoT platform. It includes firmware (https://nodemcu-build.com/) which runs on the ESP8266 Wi-Fi SoC from Espressif Systems, and hardware which is based on the ESP-12E module. The term "NodeMCU" by default refers to the firmware rather than the dev kits. The firmware uses the Lua scripting language. It is based on the eLua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
